# Fritzing sketch sample (saved by Fritzing 0.9.3b)
breadboards: 1

parts:
  tft1 = 3.2in tft touch screen
  U1 = 74HC595 [package="DIP16 [THT]"]
  U2 = 74HC595 [package="DIP16 [THT]"]
  U3 = 74HC595 [package="DIP16 [THT]"]
  U4 = 74HC595 [package="DIP16 [THT]"]
  U5 = 74HC595 [package="DIP16 [THT]"]
  Componente1 = Arduino Uno (Rev3)

nets:
  GND: tft1.GND, U1.GND, U2.GND, U3.GND, U4.GND, U5.GND, Componente1.GND
  VCC: tft1.VCC, U1.VCC, U2.VCC, U3.VCC, U4.VCC, U5.VCC, Componente1.3V3
  N1: tft1.LCD_RS, U1.Q0
  N2: tft1.LCD_WR, U1.Q1
  N3: tft1.LCD_RD, U1.Q2
  N4: tft1.LCD_DB8, U2.Q5
  N5: tft1.LCD_DB9, U2.Q6
  N6: tft1.LCD_DB10, U2.Q7
  N7: tft1.LCD_DB11, U3.Q0
  N8: tft1.LCD_DB12, U3.Q1
  N9: tft1.LCD_DB13, U3.Q2
  N10: tft1.LCD_DB14, U3.Q3
  N11: tft1.LCD_DB15, U3.Q4
  N12: tft1.LCD_CS, U1.Q3
  N13: tft1.LCD_RESET, U1.Q4
  N14: tft1.LCD_DB0, U1.Q5
  N15: tft1.LCD_DB1, U1.Q6
  N16: tft1.LCD_DB2, U1.Q7
  N17: tft1.LCD_DB3, U2.Q0
  N18: tft1.LCD_DB4, U2.Q1
  N19: tft1.LCD_DB5, U2.Q2
  N20: tft1.LCD_DB6, U2.Q3
  N21: tft1.LCD_DB7, U2.Q4
  N22: tft1.TouchP_CLK, U4.Q0
  N23: tft1.TouchP_CS, U4.Q1
  N24: tft1.TouchP_DIN, U4.Q2
  N25: tft1.NC, U4.Q3
  N26: tft1.TouchP_DOUT, U4.Q4
  N27: tft1.TouchP_Penirq, U4.Q5
  N28: tft1.SD_DOUT, U5.Q0
  N29: tft1.SD_CLK, U5.Q1
  N30: tft1.SD_DIN, U5.Q2
  N31: tft1.SD_CS, U5.Q3

custom parts:
  3.2in tft touch screen: 3.2" tft touch screen lcd display
